// Logisim project tb8.circ as structural Verilog: 1 circuit, main circuit main
module main (
  input  in_1
);

  wire AeB0, AeB1, and_1_out, and_2_out, and_3_out, and_4_out, and_5_out, and_6_out, and_7_out, and_8_out,
       and_9_out, and_10_out, and_11_out, and_12_out, and_13_out, and_14_out, and_16_out, and_17_out,
       and_18_out, and_19_out, and_20_out, and_21_out, and_22_out, and_23_out, and_24_out, and_25_out,
       and_26_out, and_28_out, and_29_out, and_30_out, and_31_out, and_33_out, and_34_out, and_37_out,
       and_38_out, and_39_out, and_40_out, and_41_out, and_42_out, and_43_out, and_44_out, and_45_out,
       and_46_out, and_47_out, and_48_out, and_49_out, and_50_out, and_51_out, and_52_out, and_53_out,
       and_54_out, and_55_out, and_56_out, and_57_out, and_58_out, and_59_out, and_60_out, and_61_out,
       and_62_out, and_63_out, and_64_out, and_65_out, and_66_out, and_67_out, and_68_out, and_69_out,
       and_70_out, and_71_out, and_72_out, and_73_out, and_74_out, and_75_out, and_76_out, and_77_out,
       and_78_out, and_79_out, and_80_out, and_81_out, and_82_out, and_83_out, and_84_out, and_85_out,
       and_86_out, and_87_out, and_88_out, and_89_out, and_90_out, and_91_out, and_92_out, and_93_out,
       and_94_out, and_95_out, and_96_out, and_97_out, and_98_out, and_99_out, and_100_out, and_101_out,
       and_102_out, and_103_out, and_104_out, and_105_out, and_106_out, and_107_out, and_108_out,
       and_109_out, and_110_out, and_111_out, and_112_out, and_113_out, C, CCLK, cef, clp, Cn, Cn4_0, Cn4_1,
       CnX, CnY, CnZ, CPL, EQL, EXC, G, G0, G1, ld, ldi_t, m, n74193_1_pin4, n74193_1_pin12, n74193_1_pin13,
       n74193_2_pin4, n74193_2_pin5, n74193_2_pin12, n74193_2_pin13, nand_1_out, nand_2_out, nand_3_out,
       nand_4_out, nand_5_out, nand_6_out, nand_9_out, nand_11_out, nand_13_out, nor_1_out, nor_2_out,
       nor_3_out, nor_4_out, nor_6_out, nor_7_out, nor_9_out, nor_10_out, nor_11_out, nor_12_out, nor_13_out,
       nor_15_out, nor_16_out, nor_17_out, nor_18_out, nor_19_out, nor_20_out, nor_22_out, nor_23_out,
       nor_24_out, nor_25_out, nor_26_out, nor_28_out, nor_30_out, not_1_out, not_2_out, not_3_out,
       not_4_out, not_5_out, not_6_out, not_7_out, not_8_out, not_9_out, not_10_out, not_11_out, not_12_out,
       not_13_out, not_14_out, not_15_out, not_16_out, not_17_out, not_18_out, not_19_out, not_20_out,
       not_21_out, or_1_out, or_2_out, or_3_out, or_7_out, P, P0, P1, R, R_al, RD, s0, s1, s2, s3,
       s_r_ff_1_q, s_r_ff_2_q, st, ste, T_RD, T_RDI, T_WR, TADR0, TADR1, TADR2, TADR3, TADR4, TADR5, TADR6,
       TADR7, WR;
  wire [3:0] dipswitch_1_sw4, dipswitch_1_sw8;
  wire [5:0] T_ADR;
  wire [7:0] a, Acc_q, alu, b, CHI, CHO, CLI, CLO, DATA, dipswitch_2_sw8, register_2_q, register_3_q,
       register_6_q, T_BUS, undriven;
  wire [7:4] Control_q;
  wire [7:6] register_1_q;
  wire [15:0] ADDRESS;

  nand nand_1 (nand_1_out, TADR2, T_WR);
  nand nand_2 (nand_2_out, TADR3, T_WR);
  nand nand_3 (nand_3_out, Cn, not_2_out);
  nand nand_4 (nand_4_out, CnX, not_3_out);
  not not_1 (not_1_out, Cn);
  D_Flip_Flop d_ff_1 (.D(CCLK), .clk(C), .Q(EXC), .Qn(CCLK), .reset(R));  // open: preset
  Register #(.trigger("high")) register_1 (.D(DATA), .en(1'b1), .clk(CCLK), .Q({register_1_q, T_ADR}), .clr(R));
  Register #(.trigger("low")) register_2 (.D(T_BUS), .en(1'b1), .clk(nand_1_out), .Q(register_2_q), .clr(R));
  Register #(.trigger("low")) register_3 (.D(T_BUS), .en(1'b1), .clk(nand_2_out), .Q(register_3_q), .clr(R));
  not not_2 (not_2_out, m);
  and and_1 (and_1_out, a[0], a[0]);
  xor xor_1 (alu[0], nand_3_out, and_9_out);
  not not_3 (not_3_out, m);
  and and_2 (and_2_out, a[4], a[4]);
  xor xor_2 (alu[4], nand_4_out, and_13_out);
  and and_3 (and_3_out, G0, P0);
  Decoder #(.enable("false"), .select(2)) decoder_1 (
    .out0(ld), .out1(ldi_t), .out2(st), .out3(ste), .sel(register_1_q));
  assign T_BUS = and_4_out ? register_2_q : 8'bz;  // Controlled_Buffer controlled_buffer_1
  and and_4 (and_4_out, TADR2, T_RD);
  assign ADDRESS[7:0] = or_1_out ? register_2_q : 8'bz;  // Controlled_Buffer controlled_buffer_2
  or or_1 (or_1_out, and_37_out, and_38_out);
  assign ADDRESS[15:8] = or_1_out ? register_3_q : 8'bz;  // Controlled_Buffer controlled_buffer_3
  assign T_BUS = and_5_out ? register_3_q : 8'bz;  // Controlled_Buffer controlled_buffer_4
  and and_5 (and_5_out, TADR3, T_RD);
  and and_6 (and_6_out, b[0], s0);
  and and_7 (and_7_out, s1, not_6_out);
  nor nor_1 (nor_1_out, and_1_out, and_6_out, and_7_out);
  not not_4 (not_4_out, nor_1_out);
  and and_8 (and_8_out, not_2_out, nor_1_out);
  and and_9 (and_9_out, not_4_out, nor_6_out);
  nor nor_2 (nor_2_out, and_8_out, and_17_out);
  and and_10 (and_10_out, b[4], s0);
  and and_11 (and_11_out, s1, not_7_out);
  nor nor_3 (nor_3_out, and_2_out, and_10_out, and_11_out);
  not not_5 (not_5_out, nor_3_out);
  and and_12 (and_12_out, not_3_out, nor_3_out);
  and and_13 (and_13_out, not_5_out, nor_7_out);
  nor nor_4 (nor_4_out, and_12_out, and_19_out);
  and and_14 (and_14_out, not_1_out, G0);
  nor nor_5 (CnX, and_3_out, and_14_out);
  assign T_BUS = T_RDI ? {2'b00, T_ADR} : 8'bz;  // Controlled_Buffer controlled_buffer_5
  and and_15 (T_RDI, ldi_t, EXC);
  not not_6 (not_6_out, b[0]);
  and and_16 (and_16_out, not_6_out, s2, a[0]);
  nor nor_6 (nor_6_out, and_16_out, and_23_out);
  and and_17 (and_17_out, not_2_out, nor_6_out, Cn);
  xor xor_3 (alu[1], nor_2_out, and_26_out);
  not not_7 (not_7_out, b[4]);
  and and_18 (and_18_out, not_7_out, s2, a[4]);
  nor nor_7 (nor_7_out, and_18_out, and_28_out);
  and and_19 (and_19_out, not_3_out, nor_7_out, CnX);
  xor xor_4 (alu[5], nor_4_out, and_31_out);
  and and_20 (and_20_out, G1, P1);
  and and_21 (and_21_out, G0, G1, P0);
  nor nor_8 (CnY, and_20_out, and_21_out, and_33_out);
  and and_22 (and_22_out, EQL, ste);
  nor nor_9 (nor_9_out, T_ADR[3], T_ADR[4], T_ADR[5]);
  Decoder #(.select(3)) decoder_2 (
    .out0(TADR0), .out1(TADR1), .sel(T_ADR[2:0]), .en(nor_9_out));  // open: out2, out3, out4, out5, out6, out7
  and and_23 (and_23_out, a[0], b[0], s3);
  and and_24 (and_24_out, a[1], a[1]);
  not not_8 (not_8_out, nor_10_out);
  and and_25 (and_25_out, not_2_out, nor_10_out);
  and and_26 (and_26_out, not_8_out, nor_15_out);
  and and_27 (AeB0, alu[0], alu[1], alu[2], alu[3]);
  and and_28 (and_28_out, a[4], b[4], s3);
  and and_29 (and_29_out, a[5], a[5]);
  not not_9 (not_9_out, nor_12_out);
  and and_30 (and_30_out, not_3_out, nor_12_out);
  and and_31 (and_31_out, not_9_out, nor_16_out);
  and and_32 (AeB1, alu[4], alu[5], alu[6], alu[7]);
  and and_33 (and_33_out, not_1_out, G0, G1);
  and and_34 (and_34_out, 1'b0, 1'b0);
  or or_2 (or_2_out, and_22_out, st);
  and and_35 (T_WR, or_2_out, EXC);
  and and_36 (T_RD, EXC, ld);
  assign DATA = and_37_out ? T_BUS : 8'bz;  // Controlled_Buffer controlled_buffer_6
  and and_37 (and_37_out, TADR4, T_WR);
  assign T_BUS = and_38_out ? DATA : 8'bz;  // Controlled_Buffer controlled_buffer_7
  and and_38 (and_38_out, TADR4, T_RD);
  and and_39 (and_39_out, b[1], s0);
  nor nor_10 (nor_10_out, and_24_out, and_39_out, and_47_out);
  and and_40 (and_40_out, not_2_out, nor_1_out, nor_15_out);
  nor nor_11 (nor_11_out, and_25_out, and_40_out, and_49_out);
  xor xor_5 (alu[2], nor_11_out, and_50_out);
  and and_41 (and_41_out, b[5], s0);
  nor nor_12 (nor_12_out, and_29_out, and_41_out, and_51_out);
  and and_42 (and_42_out, not_3_out, nor_3_out, nor_16_out);
  nor nor_13 (nor_13_out, and_30_out, and_42_out, and_53_out);
  xor xor_6 (alu[6], nor_13_out, and_54_out);
  and and_43 (and_43_out, G1, 1'b0, P1);
  and and_44 (and_44_out, G0, G1, 1'b0, P0);
  nor nor_14 (CnZ, and_34_out, and_43_out, and_44_out, and_55_out);
  Register #(.trigger("high")) register_4 (.D(T_BUS), .en(1'b1), .clk(and_45_out), .Q(CLI), .clr(R));
  and and_45 (and_45_out, TADR0, T_WR);
  Register #(.trigger("high")) register_5 (.D(T_BUS), .en(1'b1), .clk(and_46_out), .Q(CHI), .clr(R));
  and and_46 (and_46_out, T_WR, TADR1);
  not not_10 (not_10_out, b[1]);
  and and_47 (and_47_out, s1, not_10_out);
  and and_48 (and_48_out, not_10_out, s2, a[1]);
  not not_11 (not_11_out, nor_17_out);
  and and_49 (and_49_out, not_2_out, Cn, nor_6_out, nor_15_out);
  and and_50 (and_50_out, not_11_out, nor_22_out);
  not not_12 (not_12_out, b[5]);
  and and_51 (and_51_out, s1, not_12_out);
  and and_52 (and_52_out, not_12_out, s2, a[5]);
  not not_13 (not_13_out, nor_19_out);
  and and_53 (and_53_out, not_3_out, CnX, nor_7_out, nor_16_out);
  and and_54 (and_54_out, not_13_out, nor_23_out);
  and and_55 (and_55_out, not_1_out, G0, G1, 1'b0);
  S_R_Flip_Flop #(.trigger("high")) s_r_ff_1 (
    .Q(s_r_ff_1_q), .preset(and_45_out), .reset(and_62_out));  // open: S, clk, R, Qn
  S_R_Flip_Flop #(.trigger("high")) s_r_ff_2 (
    .Q(s_r_ff_2_q), .preset(and_46_out), .reset(and_62_out));  // open: S, clk, R, Qn
  and and_56 (and_56_out, a[1], s3, b[1]);
  nor nor_15 (nor_15_out, and_48_out, and_56_out);
  and and_57 (and_57_out, not_2_out, nor_17_out);
  and and_58 (and_58_out, a[5], s3, b[5]);
  nor nor_16 (nor_16_out, and_52_out, and_58_out);
  and and_59 (and_59_out, not_3_out, nor_19_out);
  and and_60 (and_60_out, 1'b0, 1'b0);
  or or_3 (or_3_out, T_RD, T_RDI);
  and and_61 (and_61_out, s_r_ff_1_q, s_r_ff_2_q);
  and and_62 (and_62_out, and_61_out, CCLK);
  Register #(.trigger("low")) u_A (.D(T_BUS), .en(1'b1), .clk(nand_5_out), .Q(a), .clr(R));
  nand nand_5 (nand_5_out, T_WR, TADR5);
  Register #(.trigger("low")) u_B (.D(T_BUS), .en(1'b1), .clk(nand_6_out), .Q(b), .clr(R));
  nand nand_6 (nand_6_out, T_WR, TADR6);
  and and_63 (and_63_out, a[2], a[2]);
  and and_64 (and_64_out, b[2], s0);
  nor nor_17 (nor_17_out, and_63_out, and_64_out, and_75_out);
  and and_65 (and_65_out, not_2_out, nor_10_out, nor_22_out);
  and and_66 (and_66_out, not_2_out, nor_1_out, nor_15_out, nor_22_out);
  nor nor_18 (nor_18_out, and_57_out, and_65_out, and_66_out, and_76_out);
  xor xor_7 (alu[3], nor_18_out, and_86_out);
  and and_67 (and_67_out, a[6], a[6]);
  and and_68 (and_68_out, b[6], s0);
  nor nor_19 (nor_19_out, and_67_out, and_68_out, and_77_out);
  and and_69 (and_69_out, not_3_out, nor_12_out, nor_23_out);
  and and_70 (and_70_out, not_3_out, nor_3_out, nor_16_out, nor_23_out);
  nor nor_20 (nor_20_out, and_59_out, and_69_out, and_70_out, and_78_out);
  xor xor_8 (alu[7], nor_20_out, and_89_out);
  and and_71 (and_71_out, 1'b0, 1'b0, 1'b0);
  and and_72 (and_72_out, G1, 1'b0, 1'b0, P1);
  nor nor_21 (G, and_60_out, and_71_out, and_72_out, and_79_out);
  Register #(.trigger("high")) register_6 (.D(T_BUS), .en(1'b1), .clk(or_3_out), .Q(register_6_q), .clr(R));
  nand nand_7 (CPL, EXC, and_61_out);
  assign T_BUS = and_73_out ? a : 8'bz;  // Controlled_Buffer controlled_buffer_8
  and and_73 (and_73_out, TADR5, T_RD);
  assign T_BUS = and_74_out ? b : 8'bz;  // Controlled_Buffer controlled_buffer_9
  and and_74 (and_74_out, TADR6, T_RD);
  not not_14 (not_14_out, b[2]);
  and and_75 (and_75_out, s1, not_14_out);
  and and_76 (and_76_out, not_2_out, Cn, nor_6_out, nor_15_out, nor_22_out);
  not not_15 (not_15_out, b[6]);
  and and_77 (and_77_out, s1, not_15_out);
  and and_78 (and_78_out, not_3_out, CnX, nor_7_out, nor_16_out, nor_23_out);
  and and_79 (and_79_out, G0, G1, 1'b0, 1'b0);
  assign T_BUS = T_WR ? register_6_q : 8'bz;  // Controlled_Buffer controlled_buffer_10
  and and_80 (and_80_out, T_RD, TADR0);
  assign T_BUS = and_80_out ? CLO : 8'bz;  // Controlled_Buffer controlled_buffer_11
  assign ADDRESS[7:0] = and_81_out ? CLO : 8'bz;  // Controlled_Buffer controlled_buffer_12
  and and_81 (and_81_out, CCLK, CCLK);
  and and_82 (and_82_out, T_RD, TADR1);
  assign T_BUS = and_82_out ? CHO : 8'bz;  // Controlled_Buffer controlled_buffer_13
  assign ADDRESS[15:8] = and_83_out ? CHO : 8'bz;  // Controlled_Buffer controlled_buffer_14
  and and_83 (and_83_out, CCLK, CCLK);
  and and_84 (and_84_out, not_14_out, s2, a[2]);
  and and_85 (and_85_out, a[2], s3, b[2]);
  nor nor_22 (nor_22_out, and_84_out, and_85_out);
  not not_16 (not_16_out, nor_24_out);
  and and_86 (and_86_out, not_16_out, nor_26_out);
  and and_87 (and_87_out, not_15_out, s2, a[6]);
  and and_88 (and_88_out, a[6], s3, b[6]);
  nor nor_23 (nor_23_out, and_87_out, and_88_out);
  not not_17 (not_17_out, nor_25_out);
  and and_89 (and_89_out, not_17_out, nor_28_out);
  or or_4 (P, P0, P1, 1'b0, 1'b0);
  nand nand_8 (R, R_al, R_al);
  Register #(.trigger("low")) Control (
    .D(T_BUS), .en(1'b1), .clk(nand_9_out), .Q({Control_q, s3, s2, s1, s0}), .clr(R));
  nand nand_9 (nand_9_out, T_WR, TADR7);
  Register #(.trigger("low")) Acc (.D(alu), .en(1'b1), .clk(EXC), .Q(Acc_q), .clr(R));
  and and_90 (and_90_out, a[3], a[3]);
  nand nand_10 (P0, nor_6_out, nor_15_out, nor_22_out, nor_26_out);
  nand nand_11 (nand_11_out, Cn, nor_6_out, nor_15_out, nor_22_out, nor_26_out);
  or or_5 (Cn4_0, ~nand_11_out, ~G0);  // OR_Gate
  and and_91 (and_91_out, a[7], a[7]);
  nand nand_12 (P1, nor_7_out, nor_16_out, nor_23_out, nor_28_out);
  nand nand_13 (nand_13_out, CnX, nor_7_out, nor_16_out, nor_23_out, nor_28_out);
  or or_6 (Cn4_1, ~nand_13_out, ~G1);  // OR_Gate
  RAM #(.addrWidth(6), .databus("bidir"), .trigger("high")) ram_1 (
    .addr(T_ADR), .we(and_93_out), .oe(and_92_out), .data(T_BUS));
  and and_92 (and_92_out, or_7_out, T_RD);
  and and_93 (and_93_out, T_WR, or_7_out);
  or or_7 (or_7_out, T_ADR[3], T_ADR[4], T_ADR[5]);
  assign T_BUS = and_94_out ? Acc_q : 8'bz;  // Controlled_Buffer controlled_buffer_15
  and and_94 (and_94_out, TADR7, T_RD);
  and and_95 (and_95_out, s1, not_18_out);
  and and_96 (and_96_out, b[3], s0);
  nor nor_24 (nor_24_out, and_90_out, and_96_out, and_95_out);
  and and_97 (and_97_out, nor_1_out, nor_15_out, nor_22_out, nor_26_out);
  and and_98 (and_98_out, s1, not_19_out);
  and and_99 (and_99_out, b[7], s0);
  nor nor_25 (nor_25_out, and_91_out, and_99_out, and_98_out);
  and and_100 (and_100_out, nor_3_out, nor_16_out, nor_23_out, nor_28_out);
  not not_18 (not_18_out, b[3]);
  and and_101 (and_101_out, not_18_out, s2, a[3]);
  and and_102 (and_102_out, a[3], s3, b[3]);
  nor nor_26 (nor_26_out, and_101_out, and_102_out);
  and and_103 (and_103_out, nor_10_out, nor_22_out, nor_26_out);
  and and_104 (and_104_out, nor_17_out, nor_26_out);
  nor nor_27 (G0, and_97_out, and_103_out, and_104_out, and_109_out);
  not not_19 (not_19_out, b[7]);
  and and_105 (and_105_out, not_19_out, s2, a[7]);
  and and_106 (and_106_out, a[7], s3, b[7]);
  nor nor_28 (nor_28_out, and_105_out, and_106_out);
  and and_107 (and_107_out, nor_12_out, nor_23_out, nor_28_out);
  and and_108 (and_108_out, nor_19_out, nor_28_out);
  nor nor_29 (G1, and_100_out, and_107_out, and_108_out, and_110_out);
  nor nor_30 (nor_30_out, T_ADR[3], T_ADR[4], T_ADR[5]);
  Decoder #(.select(3)) decoder_3 (
    .out2(TADR2), .out3(TADR3), .out4(TADR4), .out5(TADR5), .out6(TADR6), .out7(TADR7), .sel(T_ADR[2:0]),
    .en(nor_30_out));  // open: out0, out1
  Decoder #(.enable("false"), .select(2)) decoder_4 (
    .out0(cef), .out2(clp), .out3(m), .sel(Control_q[5:4]));  // open: out1
  and and_109 (and_109_out, nor_24_out, nor_24_out);
  and and_110 (and_110_out, nor_25_out, nor_25_out);
  _74193 #(.ShowInternalStructure("true")) u_74193_1 (
    .pin1(CLI[1]), .pin2(CLO[1]), .pin3(CLO[0]), .pin4(n74193_1_pin4), .pin5(CCLK), .pin6(CLO[2]),
    .pin7(CLO[3]), .pin15(CLI[0]), .pin14(R), .pin13(n74193_1_pin13), .pin12(n74193_1_pin12), .pin11(CPL),
    .pin10(CLI[2]), .pin9(CLI[3]));
  _74193 #(.ShowInternalStructure("true")) u_74193_2 (
    .pin1(CHI[1]), .pin2(CHO[1]), .pin3(CHO[0]), .pin4(n74193_2_pin4), .pin5(n74193_2_pin5), .pin6(CHO[2]),
    .pin7(CHO[3]), .pin15(CHI[0]), .pin14(R), .pin13(n74193_2_pin13), .pin12(n74193_2_pin12), .pin11(CPL),
    .pin10(CHI[2]), .pin9(CHI[3]));
  or or_8 (Cn, cef, and_111_out);
  // LedBar #(.inputtype("row")) ledbar_1: pin names not known; wires that end beside it: a
  // LedBar #(.inputtype("row")) ledbar_2: pin names not known; wires that end beside it: b
  // LedBar #(.inputtype("row")) ledbar_3: pin names not known; wires that end beside it: alu
  Hex_Digit_Display #(.decimalPoint("false")) hex_digit_display_1 (.value(DATA[7:4]));
  Hex_Digit_Display #(.decimalPoint("false")) hex_digit_display_2 (.value(dipswitch_1_sw4));
  DipSwitch dipswitch_1 (
    .sw1(dipswitch_1_sw4[3]), .sw2(dipswitch_1_sw4[2]), .sw3(dipswitch_1_sw4[1]), .sw4(dipswitch_1_sw4[0]),
    .sw5(dipswitch_1_sw8[3]), .sw6(dipswitch_1_sw8[2]), .sw7(dipswitch_1_sw8[1]), .sw8(dipswitch_1_sw8[0]));
  RAM #(.addrWidth(16), .databus("bidir"), .trigger("high")) ram_2 (
    .addr(ADDRESS), .we(not_20_out), .oe(not_21_out));  // open: clk, data
  not not_20 (not_20_out, WR);
  not not_21 (not_21_out, RD);
  and and_111 (and_111_out, clp, CnY);
  Comparator #(.mode("unsigned")) comparator_1 (.a(a), .b(b), .eq(EQL));  // open: gt, lt
  Hex_Digit_Display #(.decimalPoint("false")) hex_digit_display_3 (.value(DATA[3:0]));
  Hex_Digit_Display #(.decimalPoint("false")) hex_digit_display_4 (.value(dipswitch_1_sw8));
  Hex_Digit_Display #(.decimalPoint("false")) hex_digit_display_5 (.value(a[7:4]));
  Hex_Digit_Display #(.decimalPoint("false")) hex_digit_display_6 (.value(b[7:4]));
  Hex_Digit_Display #(.decimalPoint("false")) hex_digit_display_7 (.value(alu[7:4]));
  Hex_Digit_Display #(.decimalPoint("false")) hex_digit_display_8 (.value(ADDRESS[15:12]));
  Clock clock_1 (.out(C));
  Button #(.press("passive")) button_1 (.out(R_al));
  Hex_Digit_Display #(.decimalPoint("false")) hex_digit_display_9 (.value(a[3:0]));
  Hex_Digit_Display #(.decimalPoint("false")) hex_digit_display_10 (.value(b[3:0]));
  Hex_Digit_Display #(.decimalPoint("false")) hex_digit_display_11 (.value(alu[3:0]));
  _74193 #(.ShowInternalStructure("true")) u_74193_3 (
    .pin1(CLI[5]), .pin2(CLO[5]), .pin3(CLO[4]), .pin4(n74193_1_pin13), .pin5(n74193_1_pin12), .pin6(CLO[6]),
    .pin7(CLO[7]), .pin15(CLI[4]), .pin14(R), .pin13(n74193_2_pin4), .pin12(n74193_2_pin5), .pin11(CPL),
    .pin10(CLI[6]), .pin9(CLI[7]));
  _74193 #(.ShowInternalStructure("true")) u_74193_4 (
    .pin1(CHI[5]), .pin2(CHO[5]), .pin3(CHO[4]), .pin4(n74193_2_pin13), .pin5(n74193_2_pin12), .pin6(CHO[6]),
    .pin7(CHO[7]), .pin15(CHI[4]), .pin14(R), .pin11(CPL), .pin10(CHI[6]), .pin9(CHI[7]));  // open: pin13, pin12
  Hex_Digit_Display #(.decimalPoint("false")) hex_digit_display_12 (.value(ADDRESS[11:8]));
  Hex_Digit_Display #(.decimalPoint("false")) hex_digit_display_13 (.value(ADDRESS[7:4]));
  Hex_Digit_Display #(.decimalPoint("false")) hex_digit_display_14 (.value(T_BUS[7:4]));
  nor nor_31 (RD, CCLK, and_112_out);
  and and_112 (and_112_out, TADR4, T_RD);
  nor nor_32 (WR, and_113_out, and_113_out);
  and and_113 (and_113_out, TADR4, T_WR);
  Hex_Digit_Display #(.decimalPoint("false")) hex_digit_display_15 (.value(ADDRESS[3:0]));
  Hex_Digit_Display #(.decimalPoint("false")) hex_digit_display_16 (.value(T_BUS[3:0]));
  Multiplexer #(.width(8)) multiplexer_1 (.in0(undriven), .in1(dipswitch_2_sw8), .out(DATA), .sel(in_1));
  DipSwitch dipswitch_2 (
    .sw1(dipswitch_2_sw8[7]), .sw2(dipswitch_2_sw8[6]), .sw3(dipswitch_2_sw8[5]), .sw4(dipswitch_2_sw8[4]),
    .sw5(dipswitch_2_sw8[3]), .sw6(dipswitch_2_sw8[2]), .sw7(dipswitch_2_sw8[1]), .sw8(dipswitch_2_sw8[0]));
  // also tied to VCC on the sheet: n74193_1_pin4

  // Other names for the same wires on the sheet: ADRL[7:0] = ADDRESS[7:0]; ADRH[7:0] = ADDRESS[15:8]; F0 = alu[0];
  //   F1 = alu[1]; F2 = alu[2]; F3 = alu[3]; F4 = alu[4]; F5 = alu[5]; F6 = alu[6]; F7 = alu[7]; LDI = CCLK

  // Notes on the sheet:
  //   State Machine
  //   Instruction Decoder
  //   Address Pointer
  //   Control Unit
  //   IMM
  //   Load/Store Unit
  //   74182
  //   Conditional Logic
  //   4 WR
  //   4 RD
  //   Program Counter
  //   5 WR
  //   6 WR
  //   74181
  //   74181
  //   Transport Buffer
  //   5 RD
  //   6 RD
  //   /Reset
  //   ALU Unit
  //   7 WR
  //   Register Unit
  //   Register File
  //   Main T_ADR Decoding
  //   Split as needed on unit cards
  //   Cn Control
  //   Comparator
  //   74193 16-bit PC
  //   External Connections
  //   Backplane Logic
  //   R/W Logic
  //   Address Byte Joining
endmodule
